# Fritzing sketch wiring (saved by Fritzing 0.9.3b)
breadboards: 1

parts:
  Raspberry_Pi1 = Raspberry Pi B+
  LED1 = LED - 5mm [color="Red (633nm)" package="5 mm [THT]"]
  R1 = Resistor [tolerance=±5% resistance=220 package=THT]

nets:
  N1: Raspberry_Pi1.GPIO17, LED1.cathode
  N2: Raspberry_Pi1.GND, R1.Pin_1
  N3: LED1.anode, R1.Pin_0

notes:
  GPIO17
  GND
